// Logisim project DEMI-additionneur.circ as structural Verilog: 1 circuit, main circuit main
module main (
  input  a0,
  input  b0,
  output s0,
  output r0
);

  xor xor_1 (s0, a0, b0);
  and and_1 (r0, a0, b0);
endmodule
