// Logisim project Feutricoloreamelio.circ as structural Verilog: 1 circuit, main circuit main
module main (
);

  wire and_1_out, and_2_out, clock_1_out, nand_1_out, not_1_out;
  wire [2:0] counter_1_q;

  Clock clock_1 (.out(clock_1_out));
  Counter #(.width(3), .max('h7)) counter_1 (.Q(counter_1_q), .clk(clock_1_out));  // open: load, D, count, carry, clr
  not not_1 (not_1_out, counter_1_q[2]);
  nand nand_1 (nand_1_out, counter_1_q[1], counter_1_q[0]);
  and and_1 (and_1_out, counter_1_q[0], counter_1_q[1]);
  LED led_1 (.in(counter_1_q[2]));
  and and_2 (and_2_out, not_1_out, and_1_out);
  LED led_2 (.in(and_2_out));
  LED led_3 ();  // open: in
  // AND_Gate and_3 is placed but not wired
  LED led_4 (.in(not_1_out));
  LED led_5 ();  // open: in
  LED led_6 ();  // open: in

  // Notes on the sheet:
  //   r1
  //   o1
  //   v1
  //   r2
  //   o2
  //   v2
  //   B0
  //   B1
  //   B2
  //   NB2
  //   NB1B0
endmodule
