// Logisim project Add-Complet.circ as structural Verilog: 1 circuit, main circuit main
module main (
  input  r0,
  input  a1,
  input  b1,
  output s1,
  output r1
);

  wire and_1_out, and_2_out, xor_1_out;

  xor xor_1 (xor_1_out, a1, b1);
  and and_1 (and_1_out, a1, b1);
  and and_2 (and_2_out, r0, xor_1_out);
  xor xor_2 (s1, r0, xor_1_out);
  or or_1 (r1, and_2_out, and_1_out);
endmodule
